# Fritzing sketch EEZYbotARM_Mk2 (saved by Fritzing 0.9.4)
circuit board: 6.88566cm x 5.36311cm
breadboards: 1

parts:
  HC_05 = Bluetooth HC-05 Macho
  Servo_3 = Basic Servo
  Servo_1 = Basic Servo
  R1 = Resistor [tolerance=±5% resistance=1k package=THT]
  R2 = Resistor [tolerance=±5% resistance=2k package=THT]
  Arduino_UNO = Arduino Uno (Rev3)
  Power_5V = Power plug
  Servo_2 = Basic Servo

nets:
  N1: HC_05.State, Arduino_UNO.D4
  N2: HC_05.TXD, Arduino_UNO.D7
  N3: HC_05.RXD, R1.Pin_1, R2.Pin_0
  VCC: HC_05.VCC, Arduino_UNO.5V
  N4: HC_05.Key, Arduino_UNO.3V3
  GND: HC_05.GND, Servo_3.gnd, Servo_1.gnd, R2.Pin_1, Arduino_UNO.GND, Power_5V.GND, Servo_2.gnd
  VCC_2: Servo_3.vcc, Servo_1.vcc, Power_5V.VCC, Servo_2.vcc
  N5: Servo_3.pulse, Arduino_UNO.D8
  N6: Servo_1.pulse, Arduino_UNO.D10_PWM/SS
  N7: R1.Pin_0, Arduino_UNO.D6_PWM
  N8: Arduino_UNO.D9_PWM, Servo_2.pulse

notes:
  Ground between Arduino and Servos to prevent jittering.
  (grey cables)
  5V
  VCC
  GND
  TX
  RX
  EN
  STATE

// code stored in the sketch: EEZYbotARM_Mk2.ino
#include <SoftwareSerial.h>
#include <Servo.h>

#define bluetoothRx 6
#define bluetoothTx 7
#define bluetoothStatePin 4

// default servo movement:
int MIN = 1000, MID = 1500, MAX = 2000;

// Bluetooth
String Name = "Servocontrol_";

// do not modify these
boolean connected = false;
boolean servosAttached = false;
SoftwareSerial HC05(bluetoothTx, bluetoothRx);
Servo myservo1, myservo2, myservo3;

//-----------------------------------
void setup()
{
  initModule();
  initServos();
  printServoInfo();
  printSettings("Default settings:");
}

void loop()
{
  checkBluetoothConnectionState();
  checkSerialInput();
  checkHC05Input();
}

// code stored in the sketch: HC05Input.ino
void checkHC05Input() {
  //Read from bluetooth and write to usb serial
  if(HC05.available() >= 2) {
    unsigned int servopos = HC05.read();
    unsigned int servopos1 = HC05.read();
    unsigned int realservo = (servopos1 * 256) + servopos; 
    
    if(realservo >= 1000 && realservo <1180){
      double servo1 = map(realservo, 1000,1180,MIN,MAX);
      myservo1.writeMicroseconds(servo1);
      delay(10);
    } 
        
    if(realservo >=2000 && realservo <2180){
      double servo2 = map(realservo,2000,2180,MIN,MAX);
      myservo2.writeMicroseconds(servo2);
      delay(10);
    }
    
    if(realservo >=3000 && realservo < 3180){
      double servo3 = map(realservo, 3000, 3180,MIN,MAX);
      myservo3.writeMicroseconds(servo3);
      delay(10);
    }
  }
}

// code stored in the sketch: Initialization.ino
void initServos() {
  Serial.println("Initialize servos...");

  if(!servosAttached) {
    Serial.println("Attaching servos...");
    myservo1.attach(8);
    myservo2.attach(9);
    myservo3.attach(10);

    servosAttached = true;
  }
  testServos();
}

void initModule() {
  Serial.begin(57600);     //Baudrate ffor communication with serial monitor
  
  Serial.println("Initialize..."); 
  Serial.println();
  
  Serial.println("Configure HC-05 Modul:"); 
  HC05.begin(38400);

  Serial.println("Reset HC-05 -> Slave mode, Baudrate 38400, Password:1234, Device-Name: 'hc01.com HC-05'");
  if(!read("AT+ORGL").startsWith("OK")) {
    Serial.println("Error!");
    return;
    //while(1);     
  }
  
  //Delete all Devices from pairing list
  if(!read("AT+RMAAD").startsWith("OK")) {
    Serial.println("Fehler!");
    while(1);     
  }
  
  //Read MAC-Adress and build bluetooth name
  String addr = read("AT+ADDR?");
  Name.concat(addr.substring(addr.lastIndexOf(":")+1,addr.lastIndexOf(":")+4));
  Serial.println(Name);
  
  //Set bluetooth name to "Servocontrol_XXX"
  String result = read("AT+NAME="+Name);
  Serial.println("Bluetooth name: " + result);
  if(!result.startsWith("OK")) {
    Serial.println("Fehler!");
    while(1);     
  }

  //Checke if Baudrate set to 38400
  if(!read("AT+UART?").startsWith("+UART:38400,0,0")) {
    Serial.println("Fehler!");
    while(1);     
  }

  //Read version of module
  String version = read("AT+VERSION?");
 
  //Restart module resetting connections
  if(!read("AT+RESET").startsWith("OK")) {
    Serial.println("Fehler!");
    while(1);     
  }
  delay(1000);  //So ein Reset dauert seine Zeit...

  //Stop all connections and make visible
  read("AT+INIT");
  read("AT+DISC");
  
  //Gibt den Status des Moduls an
  read("AT+STATE?");

  pinMode(bluetoothStatePin, INPUT);
}

String read(String Befehl){
  char rc;
  String result = "";
  HC05.println(Befehl);
  delay(500);
  
  while(HC05.available() > 0) {
    rc = HC05.read(); 
    result.concat(rc);
  }  
  return result;
}

// code stored in the sketch: SerialMonitorInput.ino
void checkSerialInput() {
  if(Serial.available() > 0) {
    String monitor_input = Serial.readStringUntil("!");
    
    if(monitor_input.startsWith("store")) {
      Serial.println("Store settings...");
      
      if(monitor_input.substring(6).startsWith("min")) {
        MIN = monitor_input.substring(10).toInt();
      } else if(monitor_input.substring(6).startsWith("max")) {
        MAX = monitor_input.substring(10).toInt();
      }
      MID = (MAX - MIN) / 2;
      printSettings("Stored settings:");
      testServos();
      
    } else if(String(monitor_input.charAt(0)).toInt() > 0 &&
              String(monitor_input.charAt(0)).toInt() < 3){
      Serial.println("Setting position...");
      String servoNo = monitor_input.substring(0,1);
      String seconds = monitor_input.substring(2);

      if(servoNo.equals("1")){
        Serial.println("---> 1");
        myservo1.writeMicroseconds(seconds.toInt());
      } else if(servoNo.equals("2")){
        Serial.println("---> 2");
        myservo2.writeMicroseconds(seconds.toInt());
      } else if(servoNo.equals("3")){
        Serial.println("---> 3");
        myservo3.writeMicroseconds(seconds.toInt());
      }
    } else {
      Serial.println("unrecognized command!");
    }

    while(Serial.available()){
      Serial.read();
    }
  }
}

// code stored in the sketch: Utils.ino
void printServoInfo() {
  Serial.println("------------------------------------");
  Serial.println("Fine tune the endpoints:");
  Serial.println("Open a serial monitor on 576000");
  Serial.println("Enter the numer of the servo followed by the microsecond value.");
  Serial.println("See: https://www.arduino.cc/en/Reference/ServoWriteMicroseconds");
  Serial.println("1 1500 -> resulting in servo 1 being set to 1500 (90°)");
  Serial.println("Store the settings:");
  Serial.println("store min|max value");
  Serial.println("e.g. 'store min 900'");
  Serial.println("To terminate the command set an exclamation mark to the end!");
  Serial.println("------------------------------------");
}

void testServos() {
  Serial.print("Testing: 0°");
  myservo1.writeMicroseconds(MIN);
  myservo2.writeMicroseconds(MIN);
  myservo3.writeMicroseconds(MIN);
  delay(2 * 1000);

  Serial.print(", 180°");
  myservo1.writeMicroseconds(MAX);
  myservo2.writeMicroseconds(MAX);
  myservo3.writeMicroseconds(MAX);
  delay(2 * 1000);

  Serial.println(", 90°");
  myservo1.writeMicroseconds(MID);
  myservo2.writeMicroseconds(MID);
  myservo3.writeMicroseconds(MID);
}

void printSettings(String text) {
  Serial.println(text
        + "\nMIN: " + String(MIN)
        + "\nMAX: " + String(MAX)
        + "\nMID: " + String(MID)
      ); 
}

void checkBluetoothConnectionState() {
  if(digitalRead(bluetoothStatePin) == HIGH && connected == false) {
    Serial.println("Connected...");
    connected = true;
  } else if(digitalRead(bluetoothStatePin) == LOW && connected == true) {
    Serial.println("Connection lost!");
    connected = false;
  }
}
